// Logisim project Conditional Branch + Subroutines + ALU.circ as structural Verilog: 1 circuit, main circuit main
module main (
  input  Clear_Global_Mem,
  input  in_2
);

  wire ALU, ALUI, and_1_out, and_2_out, beq, clk, Clock_out, comparator_1_eq, comparator_1_lt,
       comparator_2_eq, copy, decoder_2_out0, decoder_2_out1, decoder_2_out2, decoder_2_out3, decoder_3_out0,
       decoder_3_out1, decoder_3_out2, decoder_3_out3, halt, jal, load, LoadJalRegisters, multiplexer_1_out,
       not_1_out, or_1_out, or_2_out, or_3_out, RALoad, RAReturn, ReadJalRegisters, store, tty, ttyALoad,
       ttyLoad;
  wire [1:0] SubopField;
  wire [2:0] ram_1_data, regField;
  wire [6:0] multiplexer_9_out;
  wire [7:0] accOut, adder_2_out, ALUOut, divider_1_out, divider_2_rem, globalOut, imm, JALRegOut,
       multiplexer_2_out, multiplexer_6_out, multiplexer_8_out, regOut, subtractor_1_out;
  wire [15:0] adder_1_out, bit_extender_1_out, multiplexer_3_out, multiplexer_4_out, PCOut, ra_q, RAOut;

  Comparator comparator_1 (.a(regOut), .b(accOut), .eq(comparator_1_eq), .lt(comparator_1_lt));  // open: gt
  not not_1 (not_1_out, comparator_1_eq);
  Multiplexer #(.select(2), .enable("false")) multiplexer_1 (
    .in0(comparator_1_eq), .in1(not_1_out), .in2(comparator_1_lt), .out(multiplexer_1_out), .sel(SubopField));  // open: in3
  Comparator #(.width(2)) comparator_2 (.a(SubopField), .b(2'b11), .eq(comparator_2_eq));  // open: gt, lt
  assign bit_extender_1_out = {{8{imm[7]}}, imm};  // Bit_Extender bit_extender_1
  and and_1 (and_1_out, beq, multiplexer_1_out);
  or or_1 (or_1_out, and_1_out, and_2_out, RALoad);
  and and_2 (and_2_out, comparator_2_eq, beq);
  Multiplexer #(.width(8), .enable("false")) multiplexer_2 (
    .in0(imm), .in1(accOut), .out(multiplexer_2_out), .sel(ALU));
  Adder #(.width(16)) adder_1 (.a(PCOut), .b(multiplexer_3_out), .out(adder_1_out));  // open: cin, cout
  Multiplexer #(.width(16), .enable("false")) multiplexer_3 (
    .in0(16'h1), .in1(bit_extender_1_out), .out(multiplexer_3_out), .sel(or_1_out));
  Adder adder_2 (.a(regOut), .b(multiplexer_2_out), .out(adder_2_out));  // open: cin, cout
  Subtractor subtractor_1 (.a(regOut), .b(multiplexer_2_out), .out(subtractor_1_out));  // open: bin, bout
  Divider divider_1 (.a(regOut), .b(multiplexer_2_out), .out(divider_1_out));  // open: upper, rem
  Divider divider_2 (.a(regOut), .b(multiplexer_2_out), .rem(divider_2_rem));  // open: out, upper
  Multiplexer #(.width(16), .enable("false")) multiplexer_4 (
    .in0(adder_1_out), .in1(RAOut), .out(multiplexer_4_out), .sel(RAReturn));
  Multiplexer #(.select(2), .width(8), .enable("false")) multiplexer_5 (
    .in0(adder_2_out), .in1(subtractor_1_out), .in2(divider_1_out), .in3(divider_2_rem), .out(ALUOut),
    .sel(SubopField));
  Register #(.width(16)) register_1 (.D(multiplexer_4_out), .Q(PCOut), .clk(clk), .clr(in_2));  // open: en
  RAM #(.addrWidth(16), .dataWidth(16), .bus("separate")) ram_1 (
    .addr(PCOut), .data({imm, SubopField, regField, ram_1_data}), .str(1'b0), .clk(clk));  // open: din, sel, ld, clr
  RAM #(.addrWidth(3), .bus("separate")) ram_2 (
    .addr(regField), .din(accOut), .data(regOut), .str(copy), .clk(clk), .clr(in_2));  // open: sel, ld
  RAM #(.bus("separate")) ram_3 (
    .addr(ALUOut), .din(accOut), .data(globalOut), .str(store), .clk(clk), .clr(Clear_Global_Mem));  // open: sel, ld
  Decoder #(.select(3), .enable("false")) decoder_1 (
    .out0(jal), .out1(ALUI), .out2(ALU), .out3(tty), .out4(copy), .out5(beq), .out6(load), .out7(store),
    .sel(ram_1_data));
  Multiplexer #(.width(8), .enable("false")) multiplexer_6 (
    .in0(ALUOut), .in1(globalOut), .out(multiplexer_6_out), .sel(load));
  Clock Clock (.out(Clock_out));
  Multiplexer #(.enable("false")) multiplexer_7 (.in0(Clock_out), .in1(1'b0), .out(clk), .sel(halt));
  Multiplexer #(.width(8), .enable("false")) multiplexer_8 (
    .in0(multiplexer_6_out), .in1(JALRegOut), .out(multiplexer_8_out), .sel(ReadJalRegisters));
  Multiplexer #(.width(7), .enable("false")) multiplexer_9 (
    .in0(imm[6:0]), .in1(accOut[6:0]), .out(multiplexer_9_out), .sel(imm[7]));
  TTY #(.rows(9)) tty_1 (.data(multiplexer_9_out), .clk(clk), .we(or_2_out), .clr(in_2));
  or or_2 (or_2_out, ttyLoad, ttyALoad);
  or or_3 (or_3_out, ALUI, load, ALU, ReadJalRegisters);
  Decoder #(.select(2), .enable("false")) decoder_2 (
    .out0(decoder_2_out0), .out1(decoder_2_out1), .out2(decoder_2_out2), .out3(decoder_2_out3),
    .sel(SubopField));
  Register Accumulator (.D(multiplexer_8_out), .en(or_3_out), .Q(accOut), .clk(clk), .clr(in_2));
  Register #(.width(16)) ra (.D(PCOut), .en(RALoad), .Q(ra_q), .clk(clk), .clr(in_2));
  Decoder #(.select(2), .enable("false")) decoder_3 (
    .out0(decoder_3_out0), .out1(decoder_3_out1), .out2(decoder_3_out2), .out3(decoder_3_out3),
    .sel(SubopField));
  and and_3 (RALoad, decoder_2_out0, jal);
  and and_4 (RAReturn, decoder_2_out1, jal);
  and and_5 (LoadJalRegisters, decoder_2_out2, jal);
  and and_6 (ReadJalRegisters, decoder_2_out3, jal);
  Adder #(.width(16)) adder_3 (.a(ra_q), .b(16'h1), .out(RAOut));  // open: cin, cout
  and and_7 (ttyLoad, decoder_3_out0, tty);
  and and_8 (ttyALoad, decoder_3_out1, tty);
  and and_9 (halt, decoder_3_out2, tty);
  // AND_Gate and_10 has open pins: in0=decoder_3_out3, in1=tty, out=open
  RAM #(.addrWidth(3), .bus("separate")) ram_4 (
    .addr(regField), .din(accOut), .data(JALRegOut), .str(LoadJalRegisters), .clk(clk), .clr(in_2));  // open: sel, ld

  // Other names for the same wires on the sheet: rst = in_2

  // Notes on the sheet:
  //   Load TTY Code at address: 0x0021
  //   Reg + Imm -> Acc: 001 = 01
  //   Reg + Acc -> Acc: 010 = 02
  //   1 0 + 000 = load imm to subroutine registers in reg0
  //   1 1 + 000 = load subroutine register into acc from reg0
  //   Instruction RAM
  //   Register File
  //   16 Bits = [8 bits]: Immediate + 00 + [3 bits]: Register Select + [3 bits]: OP Code
  //   JSR family: 000 = 00
  //   Print Ascii: 011 = 03
  //   Acc -> Reg: 100 = 04
  //   JMP Offset: 101 = 05
  //   Load to Acc: 110 = 06
  //   Acc -> Mem: 111 = 07
  //   0 0 + 000 = jump to imm + load current PC into $ra
  //   0 1 + 000 = jump back to address stored in $ra
  //   OP Code Logic
endmodule
